// Logisim project 2301cs24_lab_2.circ as structural Verilog
module _2x4_decoder (
  input  enable,
  input  in_2,
  input  in_3,
  output y0,
  output y1,
  output y2,
  output y3
);

  wire not_1_out, not_2_out;

  not not_1 (not_1_out, in_3);
  not not_2 (not_2_out, in_2);
  and and_1 (y0, not_2_out, enable, not_1_out);
  and and_2 (y1, in_2, enable, not_1_out);
  and and_3 (y2, not_2_out, enable, in_3);
  and and_4 (y3, in_2, enable, in_3);
endmodule

module _4x2_priority_encoder (
  input  X3,
  input  X2,
  input  X1,
  input  X0,
  output Y1,
  output Y0,
  output V
);

  wire and_1_out, not_1_out;

  not not_1 (not_1_out, X2);
  or or_1 (Y1, X2, X3);
  or or_2 (V, X0, X1, X2, X3);
  and and_1 (and_1_out, not_1_out, X1);
  or or_3 (Y0, and_1_out, X3);
endmodule

module _4x1_mux (
  input  [1:0] S0_S1,
  input  enable,
  input  I0,
  input  I1,
  input  I2,
  input  I3,
  output out_7
);

  wire and_1_out, and_2_out, and_3_out, and_4_out, not_1_out, not_2_out, or_1_out;

  not not_1 (not_1_out, S0_S1[1]);
  not not_2 (not_2_out, S0_S1[0]);
  and and_1 (and_1_out, not_2_out, I0, not_1_out);
  and and_2 (and_2_out, S0_S1[0], I1, not_1_out);
  and and_3 (and_3_out, not_2_out, I2, S0_S1[1]);
  and and_4 (and_4_out, S0_S1[0], I3, S0_S1[1]);
  or or_1 (or_1_out, and_1_out, and_2_out, and_3_out, and_4_out);
  and and_5 (out_7, enable, or_1_out);
endmodule

module full_adder (
  input  A,
  input  B,
  input  C_in,
  output S,
  output C_out
);

  wire and_1_out, and_2_out, and_3_out, and_4_out, and_5_out, and_6_out, not_1_out, not_2_out, not_3_out,
       not_4_out, or_1_out;

  not not_1 (not_1_out, A);
  not not_2 (not_2_out, B);
  and and_1 (and_1_out, B, A);
  and and_2 (and_2_out, not_1_out, B);
  and and_3 (and_3_out, A, not_2_out);
  or or_1 (or_1_out, and_2_out, and_3_out);
  and and_4 (and_4_out, C_in, or_1_out);
  not not_3 (not_3_out, or_1_out);
  not not_4 (not_4_out, C_in);
  or or_2 (C_out, and_4_out, and_1_out);
  and and_5 (and_5_out, not_3_out, C_in);
  and and_6 (and_6_out, or_1_out, not_4_out);
  or or_3 (S, and_5_out, and_6_out);
endmodule

module _4_bit_adder_subtracter (
  input  [3:0] A,
  input  [3:0] B,
  input  in_3,
  output C,
  output V,
  output [3:0] OUT
);

  wire full_adder_2_c_out, full_adder_3_c_out, full_adder_4_c_out, xor_2_out, xor_3_out, xor_4_out, xor_5_out;

  xor xor_1 (V, C, full_adder_2_c_out);
  xor xor_2 (xor_2_out, B[3], in_3);
  full_adder full_adder_1 (.A(full_adder_2_c_out), .B(A[3]), .C_in(xor_2_out), .S(OUT[3]), .C_out(C));
  xor xor_3 (xor_3_out, B[2], in_3);
  full_adder full_adder_2 (.A(full_adder_3_c_out), .B(A[2]), .C_in(xor_3_out), .S(OUT[2]), .C_out(full_adder_2_c_out));
  xor xor_4 (xor_4_out, B[1], in_3);
  full_adder full_adder_3 (.A(full_adder_4_c_out), .B(A[1]), .C_in(xor_4_out), .S(OUT[1]), .C_out(full_adder_3_c_out));
  xor xor_5 (xor_5_out, B[0], in_3);
  full_adder full_adder_4 (.A(in_3), .B(A[0]), .C_in(xor_5_out), .S(OUT[0]), .C_out(full_adder_4_c_out));
endmodule

module boolean_function_1 (
  input  A,
  input  [2:0] BCD,
  output out_3
);

  wire and_1_out, decoder_1_out0, decoder_1_out1, decoder_1_out2, decoder_1_out3, decoder_1_out4,
       decoder_1_out5, decoder_1_out6, decoder_1_out7, not_2_out, not_5_out, not_7_out, not_8_out, not_9_out,
       not_10_out;

  Decoder #(.select(3), .enable("false")) decoder_1 (
    .out0(decoder_1_out0), .out1(decoder_1_out1), .out2(decoder_1_out2), .out3(decoder_1_out3),
    .out4(decoder_1_out4), .out5(decoder_1_out5), .out6(decoder_1_out6), .out7(decoder_1_out7), .sel(BCD));
  // NOT_Gate not_1 has open pins: in=decoder_1_out3, out=open
  not not_2 (not_2_out, decoder_1_out4);
  // NOT_Gate not_3 has open pins: in=decoder_1_out5, out=open
  // NOT_Gate not_4 has open pins: in=decoder_1_out6, out=open
  not not_5 (not_5_out, decoder_1_out7);
  // NOT_Gate not_6 has open pins: in=decoder_1_out0, out=open
  not not_7 (not_7_out, decoder_1_out1);
  not not_8 (not_8_out, decoder_1_out2);
  not not_9 (not_9_out, A);
  and and_1 (and_1_out, not_7_out, not_8_out, not_2_out, not_5_out);
  not not_10 (not_10_out, and_1_out);
  and and_2 (out_3, not_9_out, not_10_out);
endmodule

module _5_b (
  input  B,
  input  [2:0] ACD,
  output Y
);

  wire multiplexer_1_out;

  Multiplexer #(.enable("false")) multiplexer_1 (.in0(1'b1), .in1(1'b0), .out(multiplexer_1_out), .sel(B));
  Multiplexer #(.select(3), .enable("false")) multiplexer_2 (
    .in0(1'b1), .in1(1'b1), .in2(1'b0), .in3(B), .in4(1'b0), .in5(multiplexer_1_out), .in6(B), .in7(1'b1),
    .out(Y), .sel(ACD));

  // Notes on the sheet:
  //   F(A,B,C,D)=(0,1,4,5,7,9,11,14,15)
endmodule

module _6_a (
  input  [15:0] B,
  input  [15:0] A,
  input  [3:0] S,
  output Y
);

  wire clk_out, not_1_out;

  Clock clk (.out(clk_out));
  Multiplexer #(.select(4)) multiplexer_1 (
    .in0(A[0]), .in1(A[1]), .in2(A[2]), .in3(A[3]), .in4(A[4]), .in5(A[5]), .in6(A[6]), .in7(A[7]),
    .in8(A[8]), .in9(A[9]), .in10(A[10]), .in11(A[11]), .in12(A[12]), .in13(A[13]), .in14(A[14]),
    .in15(A[15]), .out(Y), .sel(S), .en(not_1_out));
  not not_1 (not_1_out, clk_out);
  Multiplexer #(.select(4)) multiplexer_2 (
    .in0(B[0]), .in1(B[1]), .in2(B[2]), .in3(B[3]), .in4(B[4]), .in5(B[5]), .in6(B[6]), .in7(B[7]),
    .in8(B[8]), .in9(B[9]), .in10(B[10]), .in11(B[11]), .in12(B[12]), .in13(B[13]), .in14(B[14]),
    .in15(B[15]), .out(Y), .sel(S), .en(clk_out));

  // Notes on the sheet:
  //   Group A
  //   Clock based TDM Multiplexer
  //   Group B
endmodule

module _6_b (
  input  [15:0] B,
  input  [15:0] A,
  input  [3:0] S,
  output Y
);

  wire Clk_out, not_1_out;
  wire [2:0] counter_1_q;

  Clock Clk (.out(Clk_out));
  Counter #(.width(3), .max('h7)) counter_1 (.Q(counter_1_q), .clk(Clk_out));  // open: load, D, count, carry, clr
  Multiplexer #(.select(4)) multiplexer_1 (
    .in0(A[0]), .in1(A[1]), .in2(A[2]), .in3(A[3]), .in4(A[4]), .in5(A[5]), .in6(A[6]), .in7(A[7]),
    .in8(A[8]), .in9(A[9]), .in10(A[10]), .in11(A[11]), .in12(A[12]), .in13(A[13]), .in14(A[14]),
    .in15(A[15]), .out(Y), .sel(S), .en(not_1_out));
  not not_1 (not_1_out, counter_1_q[2]);
  Multiplexer #(.select(4)) multiplexer_2 (
    .in0(B[0]), .in1(B[1]), .in2(B[2]), .in3(B[3]), .in4(B[4]), .in5(B[5]), .in6(B[6]), .in7(B[7]),
    .in8(B[8]), .in9(B[9]), .in10(B[10]), .in11(B[11]), .in12(B[12]), .in13(B[13]), .in14(B[14]),
    .in15(B[15]), .out(Y), .sel(S), .en(counter_1_q[2]));

  // Notes on the sheet:
  //   Group A
  //   Counter based TDM Multiplexer
  //   Group B
endmodule
